# Fritzing sketch Acquario (saved by Fritzing 0.9.0b)
breadboards: 1

parts:
  Componente1 = Arduino Uno (Rev3)
  S1 = Momentary Switch [package=ksa_sealed_tac_switch]
  S2 = Momentary Switch [package=ksa_sealed_tac_switch]
  S3 = Momentary Switch [package=ksa_sealed_tac_switch]
  LED1 = smd LED [color="White (4500K)" package="0805 [SMD]"]
  LED2 = smd LED [color="White (4500K)" package="0805 [SMD]"]
  LED3 = smd LED [color="White (4500K)" package="0805 [SMD]"]
  LED4 = smd LED [color="Red (633nm)" package="0805 [SMD]"]
  LED5 = smd LED [color="Red (633nm)" package="0805 [SMD]"]
  LCM1602_IIC4 = LCM1602 IIC [part_number="LCM1602 IIC" chip_label="LCM1602 IIC" package="DIP (Dual Inline) [THT]"]
  U3 = LCD-16X2 [package=lcd-16x2]
  Componente8 = Real Time Clock Module - DS1307 RTC Breakout Board
  RHT1 = Humidity and Temperature Sensor RHT03
  U4 = TEMPERATURE-SENSOR [package=to-92]
  R1 = Resistor [tolerance=±5% resistance=220 package=THT]
  R3 = Resistor [tolerance=±5% resistance=220 package=THT]
  R4 = Resistor [tolerance=±5% resistance=220 package=THT]
  R5 = Resistor [tolerance=±5% resistance=220 package=THT]
  R6 = Resistor [tolerance=±5% resistance=220 package=THT]

nets:
  N1: Componente1.A4/SDA, LCM1602_IIC4.SDA, Componente8.SDA
  N2: Componente1.A5/SCL, LCM1602_IIC4.SCL, Componente8.SCL
  N3: Componente1.D8, S1.4
  N4: Componente1.D9_PWM, R1.Pin_0
  N5: Componente1.D10_PWM/SS, R3.Pin_0
  N6: Componente1.D11_PWM/MOSI, R4.Pin_0
  N7: Componente1.D12/MISO, R5.Pin_0
  N8: Componente1.D13/SCK, R6.Pin_0
  N9: Componente1.D2, U4.ADJ
  N10: Componente1.D3_PWM, RHT1.Data-signal
  N11: Componente1.D6_PWM, S3.4
  N12: Componente1.D7, S2.4
  VCC: Componente1.5V, LCM1602_IIC4.VCC, Componente8.5V, RHT1.Vcc, U4.VCC
  GND: Componente1.GND, S1.1, S2.1, S3.1, LED1.cathode, LED2.cathode, LED3.cathode, LED4.cathode, LED5.cathode, LCM1602_IIC4.GND, Componente8.GND, RHT1.GND_2, U4.GND
  N13: LED1.anode, R4.Pin_1
  N14: LED2.anode, R3.Pin_1
  N15: LED3.anode, R1.Pin_1
  N16: LED4.anode, R6.Pin_1
  N17: LED5.anode, R5.Pin_1
  VSS: LCM1602_IIC4.VSS, U3.VSS
  VDD: LCM1602_IIC4.VDD, U3.VDD
  N18: LCM1602_IIC4.V0, U3.VO
  N19: LCM1602_IIC4.RS, U3.RS
  N20: LCM1602_IIC4.RW, U3.R_W
  N21: LCM1602_IIC4.E, U3.E
  N22: LCM1602_IIC4.D0, U3.DB0
  N23: LCM1602_IIC4.D1, U3.DB1
  N24: LCM1602_IIC4.D2, U3.DB2
  N25: LCM1602_IIC4.D3, U3.DB3
  N26: LCM1602_IIC4.D4, U3.DB4
  N27: LCM1602_IIC4.D5, U3.DB5
  N28: LCM1602_IIC4.D6, U3.DB6
  N29: LCM1602_IIC4.D7, U3.DB7
  N30: LCM1602_IIC4.A, U3.A
  N31: LCM1602_IIC4.K, U3.K
  N32: LCM1602_IIC4.LED_A, LCM1602_IIC4.LED_B

custom parts:
  LCM1602 IIC: I2C-Module to use a 1602 or 2004 LCD on with the wire.h libory Serial LCD Modul
